// Logisim project counter.circ as structural Verilog: 4 circuits, main circuit main
module main (
  input  Reset,
  output Q4,
  output Q3,
  output Q2,
  output Q1,
  output Q0
);

  wire Clk_out;

  Clock Clk (.out(Clk_out));
  mod18_dec_counter mod18_dec_counter_1 (.R(Reset), .T(Clk_out), .o_4(Q4), .o_3(Q3), .o_2(Q2), .o_1(Q1), .o_0(Q0));
endmodule

module mod18_dec_counter (
  input  R,
  input  T,
  output o_4,
  output o_3,
  output o_2,
  output o_1,
  output o_0
);

  wire and_1_out, and_2_out, and_3_out, and_4_out, and_5_out, and_6_out, and_7_out, and_8_out, and_9_out,
       and_10_out, and_11_out, and_12_out, or_1_out, t_trigger_1_nq, t_trigger_1_q, t_trigger_2_nq,
       t_trigger_2_q, t_trigger_3_nq, t_trigger_3_q, t_trigger_4_nq, t_trigger_4_q, t_trigger_5_nq;
  wire [3:0] binary_to_bcd_converter_1_p2, binary_to_bcd_converter_1_p3;

  or or_1 (or_1_out, and_1_out, R);
  T_trigger t_trigger_1 (.Clear(or_1_out), .C(T), .Preset(1'b0), .T(T), .Q(t_trigger_1_q), .nQ(t_trigger_1_nq));
  T_trigger t_trigger_2 (
    .Clear(1'b0), .C(t_trigger_1_q), .Preset(or_1_out), .T(T), .Q(t_trigger_2_q), .nQ(t_trigger_2_nq));
  T_trigger t_trigger_3 (
    .Clear(1'b0), .C(t_trigger_2_q), .Preset(or_1_out), .T(T), .Q(t_trigger_3_q), .nQ(t_trigger_3_nq));
  T_trigger t_trigger_4 (
    .Clear(1'b0), .C(t_trigger_3_q), .Preset(or_1_out), .T(T), .Q(t_trigger_4_q), .nQ(t_trigger_4_nq));
  T_trigger t_trigger_5 (.Clear(or_1_out), .C(t_trigger_4_q), .Preset(1'b0), .T(T), .nQ(t_trigger_5_nq));  // open: Q
  and and_1 (and_1_out, T, and_2_out);
  and and_2 (and_2_out, t_trigger_1_nq, t_trigger_2_nq, t_trigger_3_nq, t_trigger_4_nq, t_trigger_5_nq);
  and and_3 (and_3_out, 1'b1, and_2_out);
  or or_2 (o_4, and_3_out, and_4_out);
  and and_4 (and_4_out, ~and_2_out, t_trigger_5_nq);  // AND_Gate
  and and_5 (and_5_out, 1'b0, and_2_out);
  or or_3 (o_3, and_5_out, and_6_out);
  and and_6 (and_6_out, ~and_2_out, t_trigger_4_nq);  // AND_Gate
  and and_7 (and_7_out, 1'b0, and_2_out);
  or or_4 (o_2, and_7_out, and_8_out);
  and and_8 (and_8_out, ~and_2_out, t_trigger_3_nq);  // AND_Gate
  and and_9 (and_9_out, 1'b0, and_2_out);
  or or_5 (o_1, and_9_out, and_10_out);
  and and_10 (and_10_out, ~and_2_out, t_trigger_2_nq);  // AND_Gate
  and and_11 (and_11_out, 1'b1, and_2_out);
  or or_6 (o_0, and_11_out, and_12_out);
  and and_12 (and_12_out, ~and_2_out, t_trigger_1_nq);  // AND_Gate
  Hex_Digit_Display hex_digit_display_1 (.value(binary_to_bcd_converter_1_p2));  // open: dp
  Hex_Digit_Display hex_digit_display_2 (.value(binary_to_bcd_converter_1_p3));  // open: dp
  // Binary_to_BCD_converter #(.binvalue(5)) binary_to_bcd_converter_1: pin names not known; wires that end beside it: and_3_out, binary_to_bcd_converter_1_p2, binary_to_bcd_converter_1_p3

  // Notes on the sheet:
  //   0
  //   1
  //   2
  //   3
  //   4
endmodule

module T_trigger (
  input  Preset,
  input  T,
  input  C,
  input  Clear,
  output Q,
  output nQ
);

  wire and_1_out, and_2_out, not_1_out, rs_trigger_1_nq, rs_trigger_1_q;

  and and_1 (and_1_out, nQ, T, C);
  and and_2 (and_2_out, C, T, Q);
  not not_1 (not_1_out, C);
  RS_trigger rs_trigger_1 (
    .Preset(Preset), .S(and_1_out), .C(C), .R(and_2_out), .Clear(Clear), .Q(rs_trigger_1_q),
    .nQ(rs_trigger_1_nq));
  RS_trigger rs_trigger_2 (
    .Preset(Preset), .S(rs_trigger_1_q), .C(not_1_out), .R(rs_trigger_1_nq), .Clear(Clear), .Q(Q), .nQ(nQ));
endmodule

module RS_trigger (
  input  Preset,
  input  S,
  input  C,
  input  R,
  input  Clear,
  output Q,
  output nQ
);

  wire nand_1_out, nand_2_out, not_1_out, not_2_out, or_1_out, por_1_out;

  not not_1 (not_1_out, Preset);
  POR por_1 (.out(por_1_out));
  nand nand_1 (nand_1_out, S, C);
  nand nand_2 (nand_2_out, C, R);
  or or_1 (or_1_out, Clear, por_1_out);
  not not_2 (not_2_out, or_1_out);
  nand nand_3 (Q, not_1_out, nand_1_out, nQ);
  nand nand_4 (nQ, Q, nand_2_out, not_2_out);
endmodule
