// Logisim project lfsr.circ as structural Verilog: 3 circuits, main circuit main
module main (
  input  in_1,
  input  in_2,
  input  in_3,
  input  in_4,
  input  in_5,
  input  in_6,
  input  in_7,
  input  in_8,
  input  in_9,
  input  in_10,
  input  in_11,
  input  in_12,
  input  in_13
);

  wire clock_1_out;
  wire [11:0] fibonacci_1_out_15;

  Clock clock_1 (.out(clock_1_out));
  Fibonacci fibonacci_1 (
    .in_1(in_8), .in_2(in_9), .in_3(in_10), .in_4(in_11), .in_5(in_12), .in_6(in_13), .S(in_1),
    .Clk(clock_1_out), .in_9(in_2), .in_10(in_3), .in_11(in_4), .in_12(in_5), .in_13(in_6), .in_14(in_7),
    .out_15(fibonacci_1_out_15));
  LedBar #(.matrixcols(12)) ledbar_1 (
    .led0(fibonacci_1_out_15[11]), .led1(fibonacci_1_out_15[10]), .led2(fibonacci_1_out_15[9]),
    .led3(fibonacci_1_out_15[8]), .led4(fibonacci_1_out_15[7]), .led5(fibonacci_1_out_15[6]),
    .led6(fibonacci_1_out_15[5]), .led7(fibonacci_1_out_15[4]), .led8(fibonacci_1_out_15[3]),
    .led9(fibonacci_1_out_15[2]), .led10(fibonacci_1_out_15[1]), .led11(fibonacci_1_out_15[0]));
endmodule

module D_trigger (
  input  Preset,
  input  D,
  input  C,
  input  Clear,
  output Q,
  output nQ
);

  wire nand_1_out, nand_2_out, nand_3_out, nand_4_out, nand_5_out, nand_6_out, not_1_out, not_2_out,
       not_3_out, not_4_out, or_1_out, por_1_out;

  not not_1 (not_1_out, Preset);
  not not_2 (not_2_out, D);
  POR por_1 (.out(por_1_out));
  nand nand_1 (nand_1_out, nQ, D, C);
  nand nand_2 (nand_2_out, C, not_2_out, Q);
  or or_1 (or_1_out, Clear, por_1_out);
  not not_3 (not_3_out, or_1_out);
  not not_4 (not_4_out, C);
  nand nand_3 (nand_3_out, not_1_out, nand_1_out, nand_4_out);
  nand nand_4 (nand_4_out, nand_3_out, nand_2_out, not_3_out);
  nand nand_5 (nand_5_out, nand_3_out, not_4_out);
  nand nand_6 (nand_6_out, not_4_out, nand_4_out);
  nand nand_7 (Q, not_1_out, nand_5_out, nQ);
  nand nand_8 (nQ, Q, nand_6_out, not_3_out);
endmodule

module Fibonacci (
  input  in_1,
  input  in_2,
  input  in_3,
  input  in_4,
  input  in_5,
  input  in_6,
  input  S,
  input  Clk,
  input  in_9,
  input  in_10,
  input  in_11,
  input  in_12,
  input  in_13,
  input  in_14,
  output [11:0] out_15
);

  wire and_1_out, and_2_out, and_3_out, and_4_out, and_5_out, and_6_out, and_7_out, and_8_out, and_9_out,
       and_10_out, and_11_out, and_12_out, and_13_out, and_14_out, and_15_out, and_16_out, and_17_out,
       and_18_out, and_19_out, and_20_out, and_21_out, and_22_out, and_23_out, and_24_out, not_1_out,
       not_2_out, not_3_out, not_4_out, not_5_out, not_6_out, not_7_out, not_8_out, not_9_out, not_10_out,
       not_11_out, not_12_out, xor_1_out, xor_2_out;
  wire [3:0] binary_to_bcd_converter_1_p2, binary_to_bcd_converter_1_p3, binary_to_bcd_converter_1_p4,
       binary_to_bcd_converter_1_p5;

  xor xor_1 (xor_1_out, out_15[9], out_15[0]);
  xor xor_2 (xor_2_out, out_15[11], xor_1_out);
  not not_1 (not_1_out, and_1_out);
  and and_1 (and_1_out, in_6, S);
  not not_2 (not_2_out, and_2_out);
  and and_2 (and_2_out, in_14, S);
  and and_3 (and_3_out, not_1_out, S);
  and and_4 (and_4_out, not_2_out, S);
  D_trigger d_trigger_1 (.Preset(and_1_out), .D(xor_2_out), .C(Clk), .Clear(and_3_out), .Q(out_15[0]));  // open: nQ
  D_trigger d_trigger_2 (.Preset(and_2_out), .D(out_15[5]), .C(Clk), .Clear(and_4_out), .Q(out_15[6]));  // open: nQ
  and and_5 (and_5_out, in_5, S);
  and and_6 (and_6_out, in_13, S);
  not not_3 (not_3_out, and_5_out);
  and and_7 (and_7_out, not_3_out, S);
  not not_4 (not_4_out, and_6_out);
  and and_8 (and_8_out, not_4_out, S);
  D_trigger d_trigger_3 (.Preset(and_5_out), .D(out_15[0]), .C(Clk), .Clear(and_7_out), .Q(out_15[1]));  // open: nQ
  D_trigger d_trigger_4 (.Preset(and_6_out), .D(out_15[6]), .C(Clk), .Clear(and_8_out), .Q(out_15[7]));  // open: nQ
  and and_9 (and_9_out, in_4, S);
  and and_10 (and_10_out, in_12, S);
  not not_5 (not_5_out, and_9_out);
  and and_11 (and_11_out, not_5_out, S);
  not not_6 (not_6_out, and_10_out);
  and and_12 (and_12_out, not_6_out, S);
  D_trigger d_trigger_5 (.Preset(and_9_out), .D(out_15[1]), .C(Clk), .Clear(and_11_out), .Q(out_15[2]));  // open: nQ
  D_trigger d_trigger_6 (.Preset(and_10_out), .D(out_15[7]), .C(Clk), .Clear(and_12_out), .Q(out_15[8]));  // open: nQ
  and and_13 (and_13_out, in_3, S);
  and and_14 (and_14_out, in_11, S);
  not not_7 (not_7_out, and_13_out);
  and and_15 (and_15_out, not_7_out, S);
  not not_8 (not_8_out, and_14_out);
  and and_16 (and_16_out, not_8_out, S);
  D_trigger d_trigger_7 (.Preset(and_13_out), .D(out_15[2]), .C(Clk), .Clear(and_15_out), .Q(out_15[3]));  // open: nQ
  D_trigger d_trigger_8 (.Preset(and_14_out), .D(out_15[8]), .C(Clk), .Clear(and_16_out), .Q(out_15[9]));  // open: nQ
  and and_17 (and_17_out, in_2, S);
  and and_18 (and_18_out, in_10, S);
  not not_9 (not_9_out, and_17_out);
  and and_19 (and_19_out, not_9_out, S);
  not not_10 (not_10_out, and_18_out);
  and and_20 (and_20_out, not_10_out, S);
  D_trigger d_trigger_9 (.Preset(and_17_out), .D(out_15[3]), .C(Clk), .Clear(and_19_out), .Q(out_15[4]));  // open: nQ
  D_trigger d_trigger_10 (.Preset(and_18_out), .D(out_15[9]), .C(Clk), .Clear(and_20_out), .Q(out_15[10]));  // open: nQ
  not not_11 (not_11_out, and_21_out);
  and and_21 (and_21_out, in_1, S);
  and and_22 (and_22_out, not_11_out, S);
  not not_12 (not_12_out, and_23_out);
  and and_23 (and_23_out, in_9, S);
  and and_24 (and_24_out, not_12_out, S);
  D_trigger d_trigger_11 (.Preset(and_21_out), .D(out_15[4]), .C(Clk), .Clear(and_22_out), .Q(out_15[5]));  // open: nQ
  D_trigger d_trigger_12 (
    .Preset(and_23_out), .D(out_15[10]), .C(Clk), .Clear(and_24_out), .Q(out_15[11]));  // open: nQ
  Hex_Digit_Display hex_digit_display_1 (.value(binary_to_bcd_converter_1_p2));  // open: dp
  // Binary_to_BCD_converter #(.binvalue(12)) binary_to_bcd_converter_1: pin names not known; wires that end beside it: out_15, binary_to_bcd_converter_1_p2, binary_to_bcd_converter_1_p3, binary_to_bcd_converter_1_p4, binary_to_bcd_converter_1_p5
  Hex_Digit_Display hex_digit_display_2 (.value(binary_to_bcd_converter_1_p3));  // open: dp
  Hex_Digit_Display hex_digit_display_3 (.value(binary_to_bcd_converter_1_p4));  // open: dp
  Hex_Digit_Display hex_digit_display_4 (.value(binary_to_bcd_converter_1_p5));  // open: dp

  // Notes on the sheet:
  //   0
  //   6
  //   9
  //   5
  //   11
endmodule
